# Fritzing sketch circuit (saved by Fritzing 0.9.3b)

parts:
  Part1 = Arduino Uno (Rev3)
  2_Channel_Relay1 = 2 Channel Power Relay

nets:
  N1: Part1.D10_PWM/SS, 2_Channel_Relay1.IN2
  N2: Part1.D11_PWM/MOSI, 2_Channel_Relay1.IN1
  5V: Part1.5V, 2_Channel_Relay1.VCC
  GND: Part1.GND, 2_Channel_Relay1.GND

custom parts:
  2 Channel Power Relay: A 2 channel power relay. The module operates at 5V.
